// Logisim project P1.circ as structural Verilog
module OneBitAdder (
  input  A,
  input  B,
  input  C_IN,
  output S,
  output C_OUT
);

  wire and_1_out, and_2_out, xor_1_out;

  xor xor_1 (xor_1_out, A, B);
  xor xor_2 (S, xor_1_out, C_IN);
  and and_1 (and_1_out, C_IN, xor_1_out);
  and and_2 (and_2_out, A, B);
  or or_1 (C_OUT, and_1_out, and_2_out);
endmodule

// 0
module EightBitAdder (
  input  [7:0] A,
  input  [7:0] B,
  input  C_IN,
  output [7:0] S
);

  wire onebitadder_1_c_out, onebitadder_2_c_out, onebitadder_3_c_out, onebitadder_4_c_out,
       onebitadder_5_c_out, onebitadder_6_c_out, onebitadder_7_c_out;

  OneBitAdder onebitadder_1 (.A(A[0]), .B(B[0]), .C_IN(C_IN), .S(S[0]), .C_OUT(onebitadder_1_c_out));
  OneBitAdder onebitadder_2 (.A(A[1]), .B(B[1]), .C_IN(onebitadder_1_c_out), .S(S[1]), .C_OUT(onebitadder_2_c_out));
  OneBitAdder onebitadder_3 (.A(A[2]), .B(B[2]), .C_IN(onebitadder_2_c_out), .S(S[2]), .C_OUT(onebitadder_3_c_out));
  OneBitAdder onebitadder_4 (.A(A[3]), .B(B[3]), .C_IN(onebitadder_3_c_out), .S(S[3]), .C_OUT(onebitadder_4_c_out));
  OneBitAdder onebitadder_5 (.A(A[4]), .B(B[4]), .C_IN(onebitadder_4_c_out), .S(S[4]), .C_OUT(onebitadder_5_c_out));
  OneBitAdder onebitadder_6 (.A(A[5]), .B(B[5]), .C_IN(onebitadder_5_c_out), .S(S[5]), .C_OUT(onebitadder_6_c_out));
  OneBitAdder onebitadder_7 (.A(A[6]), .B(B[6]), .C_IN(onebitadder_6_c_out), .S(S[6]), .C_OUT(onebitadder_7_c_out));
  OneBitAdder onebitadder_8 (.A(A[7]), .B(B[7]), .C_IN(onebitadder_7_c_out), .S(S[7]));  // open: C_OUT
endmodule

module AddSub (
  input  [7:0] A,
  input  ControlAddSub,
  input  [7:0] B,
  output [7:0] RESULT
);

  wire [7:0] xor_1_out;

  xor xor_1 (xor_1_out[0], B[0], ControlAddSub);
  xor xor_2 (xor_1_out[1], B[1], ControlAddSub);
  xor xor_3 (xor_1_out[2], B[2], ControlAddSub);
  xor xor_4 (xor_1_out[3], B[3], ControlAddSub);
  xor xor_5 (xor_1_out[4], B[4], ControlAddSub);
  xor xor_6 (xor_1_out[5], B[5], ControlAddSub);
  xor xor_7 (xor_1_out[6], B[6], ControlAddSub);
  xor xor_8 (xor_1_out[7], B[7], ControlAddSub);
  EightBitAdder eightbitadder_1 (.A(A), .B(xor_1_out), .C_IN(ControlAddSub), .S(RESULT));
endmodule

module ALU (
  input  [2:0] OP,
  input  [7:0] X_IN,
  input  [7:0] Y,
  output [7:0] X_OUT
);

  wire decoder_1_out0, decoder_1_out1, decoder_1_out2, decoder_1_out3, decoder_1_out4, decoder_1_out5,
       decoder_1_out6, decoder_1_out7, or_1_out, or_2_out;
  wire [7:0] addsub_1_result, and_1_out, controlled_buffer_1_out, lshrsh_1_result, not_1_out, or_3_out,
       xor_1_out;

  Decoder #(.select(3)) decoder_1 (
    .out0(decoder_1_out0), .out1(decoder_1_out1), .out2(decoder_1_out2), .out3(decoder_1_out3),
    .out4(decoder_1_out4), .out5(decoder_1_out5), .out6(decoder_1_out6), .out7(decoder_1_out7), .sel(OP));  // open: en
  or or_1 (or_1_out, decoder_1_out1, decoder_1_out0);
  or or_2 (or_2_out, decoder_1_out3, decoder_1_out2);
  AddSub addsub_1 (.A(X_IN), .ControlAddSub(decoder_1_out1), .B(Y), .RESULT(addsub_1_result));
  LSHRSH lshrsh_1 (.LeftOrRight(decoder_1_out3), .A(X_IN), .RESULT(lshrsh_1_result));
  assign xor_1_out = X_IN ^ Y;  // XOR_Gate xor_1, 8 bits wide
  assign not_1_out = ~X_IN;  // NOT_Gate not_1, 8 bits wide
  assign and_1_out = X_IN & Y;  // AND_Gate and_1, 8 bits wide
  assign or_3_out = X_IN | Y;  // OR_Gate or_3, 8 bits wide
  assign controlled_buffer_1_out = or_2_out ? lshrsh_1_result : 8'bz;  // Controlled_Buffer controlled_buffer_1
  assign controlled_buffer_1_out = decoder_1_out4 ? xor_1_out : 8'bz;  // Controlled_Buffer controlled_buffer_2
  assign controlled_buffer_1_out = decoder_1_out5 ? not_1_out : 8'bz;  // Controlled_Buffer controlled_buffer_3
  assign controlled_buffer_1_out = decoder_1_out6 ? and_1_out : 8'bz;  // Controlled_Buffer controlled_buffer_4
  assign controlled_buffer_1_out = decoder_1_out7 ? or_3_out : 8'bz;  // Controlled_Buffer controlled_buffer_5
  Multiplexer #(.width(8)) multiplexer_1 (
    .in0(controlled_buffer_1_out), .in1(addsub_1_result), .out(X_OUT), .sel(or_1_out));

  // Notes on the sheet:
  //   000 - Add
  //   001 - Sub
  //   011 - Lsh
  //   010 - Rsh
  //   100 - XOR
  //   101 - NOT
  //   110 - AND
  //   111 - OR
endmodule

module LSHRSH (
  input  LeftOrRight,
  input  [7:0] A,
  output [7:0] RESULT
);

  Multiplexer #(.width(8)) multiplexer_1 (.in0({1'b0, A[7:1]}), .in1({A[6:0], 1'b0}), .out(RESULT), .sel(LeftOrRight));
endmodule
